// Logisim project 1510702042.circ as structural Verilog: 1 circuit, main circuit main
module main (
  input  Input_1,
  input  Input_2,
  input  Input_3,
  input  Input_4,
  input  [2:0] OPCode,
  output [1:0] Output
);

  wire adder_1_out, adder_2_out, and_1_out, and_2_out, comparator_1_eq, comparator_1_gt, comparator_1_lt,
       comparator_2_eq, comparator_2_gt, comparator_2_lt, multiplier_1_out, multiplier_2_out, not_1_out,
       not_2_out, or_1_out, or_2_out, or_3_out, or_4_out, subtractor_1_out, subtractor_2_out, xor_1_out,
       xor_2_out;

  and and_1 (and_1_out, Input_1, Input_2);
  or or_1 (or_1_out, Input_1, Input_2);
  not not_1 (not_1_out, Input_1);
  xor xor_1 (xor_1_out, Input_1, Input_2);
  Adder #(.width(1)) adder_1 (.a(Input_1), .b(Input_2), .out(adder_1_out));  // open: cin, cout
  Subtractor #(.width(1)) subtractor_1 (.a(Input_1), .b(Input_2), .out(subtractor_1_out));  // open: bin, bout
  Multiplier #(.width(1)) multiplier_1 (.a(Input_1), .b(Input_2), .out(multiplier_1_out));  // open: cin, cout
  Comparator #(.width(1)) comparator_1 (
    .a(Input_1), .b(Input_2), .gt(comparator_1_gt), .eq(comparator_1_eq), .lt(comparator_1_lt));
  and and_2 (and_2_out, Input_3, Input_4);
  or or_2 (or_2_out, Input_3, Input_4);
  not not_2 (not_2_out, Input_3);
  xor xor_2 (xor_2_out, Input_3, Input_4);
  Adder #(.width(1)) adder_2 (.a(Input_3), .b(Input_4), .out(adder_2_out));  // open: cin, cout
  Subtractor #(.width(1)) subtractor_2 (.a(Input_3), .b(Input_4), .out(subtractor_2_out));  // open: bin, bout
  Multiplier #(.width(1)) multiplier_2 (.a(Input_3), .b(Input_4), .out(multiplier_2_out));  // open: cin, cout
  Comparator #(.width(1)) comparator_2 (
    .a(Input_3), .b(Input_4), .gt(comparator_2_gt), .eq(comparator_2_eq), .lt(comparator_2_lt));
  or or_3 (or_3_out, comparator_1_gt, comparator_1_eq, comparator_1_lt);
  or or_4 (or_4_out, comparator_2_gt, comparator_2_eq, comparator_2_lt);
  LED Greater_than (.in(comparator_1_gt));
  LED Equal (.in(comparator_1_eq));
  LED Less_than (.in(comparator_1_lt));
  LED Greater_than_2 (.in(comparator_2_gt));
  LED Equal_2 (.in(comparator_2_eq));
  LED Less_than_2 (.in(comparator_2_lt));
  Multiplexer #(.select(3), .enable("false")) multiplexer_1 (
    .in0(and_1_out), .in1(or_1_out), .in2(not_1_out), .in3(xor_1_out), .in4(adder_1_out),
    .in5(subtractor_1_out), .in6(multiplier_1_out), .in7(or_3_out), .out(Output[0]), .sel(OPCode));
  Multiplexer #(.select(3), .enable("false")) multiplexer_2 (
    .in0(and_2_out), .in1(or_2_out), .in2(not_2_out), .in3(xor_2_out), .in4(adder_2_out),
    .in5(subtractor_2_out), .in6(multiplier_2_out), .in7(or_4_out), .out(Output[1]), .sel(OPCode));
endmodule
