// Logisim project one_bit_alu.circ as structural Verilog: 1 circuit, main circuit main
module main (
  input  in_1,
  input  in_2,
  input  [1:0] in_3,
  input  in_4,
  input  in_5,
  output out_6,
  output out_7,
  output out_8,
  output out_9,
  output out_10
);

  wire adder_1_out, and_1_out, comparator_1_eq, comparator_1_gt, comparator_1_lt, multiplexer_1_out,
       multiplexer_2_out, multiplier_1_out, not_1_out, or_1_out, subtractor_1_out, xor_1_out;

  not not_1 (not_1_out, in_1);
  and and_1 (and_1_out, in_1, in_2);
  or or_1 (or_1_out, in_1, in_2);
  Adder #(.width(1)) adder_1 (.a(in_1), .b(in_2), .out(adder_1_out), .cin(in_4), .cout(out_7));
  Subtractor #(.width(1)) subtractor_1 (.a(in_1), .b(in_2), .out(subtractor_1_out));  // open: bin, bout
  Multiplier #(.width(1)) multiplier_1 (.a(in_1), .b(in_2), .out(multiplier_1_out));  // open: cin, cout
  Comparator #(.width(1)) comparator_1 (
    .a(in_1), .b(in_2), .gt(comparator_1_gt), .eq(comparator_1_eq), .lt(comparator_1_lt));
  xor xor_1 (xor_1_out, in_1, in_2);
  Multiplexer #(.select(2)) multiplexer_1 (
    .in0(not_1_out), .in1(and_1_out), .in2(or_1_out), .in3(xor_1_out), .out(multiplexer_1_out), .sel(in_3));  // open: en
  Multiplexer #(.select(2)) multiplexer_2 (
    .in0(adder_1_out), .in1(subtractor_1_out), .in2(multiplier_1_out), .out(multiplexer_2_out), .sel(in_3));  // open: in3, en
  Multiplexer multiplexer_3 (.in0(multiplexer_1_out), .in1(multiplexer_2_out), .out(out_6), .sel(in_5));  // open: en
  and and_2 (out_8, in_3[0], in_5, in_3[1], comparator_1_gt);
  and and_3 (out_9, in_3[1], in_5, in_3[0], comparator_1_eq);
  and and_4 (out_10, in_3[1], in_5, in_3[0], comparator_1_lt);
endmodule
